# Fritzing sketch BoschCar (saved by Fritzing 1.0.2b)
breadboards: 1

parts:
  Part1 = Arduino Nano (Rev3.0)
  U3 = LCD-16X2 [package=lcd-16x2]  # not connected
  Mod1 = YL-99 Limit switch and LED
  M1 = fc-51 [package=THT]
  Mod2 = YL-99 Limit switch and LED
  M2 = fc-51 [package=THT]
  M3 = fc-51 [package=THT]
  M4 = fc-51 [package=THT]

nets:
  N1: Part1.D11/MOSI, Mod2.VCC
  N2: Part1.D12/MISO, Mod1.VCC
  GND: Part1.GND, Mod1.GND, M1.pin2, Mod2.GND, M2.pin2, M3.pin2, M4.pin2
  N3: Part1.5V, M1.pin3, M2.pin3, M3.pin3, M4.pin3
  N4: Part1.A3, M1.pin1
  N5: Part1.A2, M2.pin1
  N6: Part1.A1, M3.pin1
  N7: Part1.A0, M4.pin1
